// Logisim project Computer.circ as structural Verilog: 15 circuits, main circuit 8-bit computer
module Memory (
  input  [7:0] STR,
  input  [7:0] Address,
  input  WE,
  input  CLK,
  output [7:0] LDR
);

  wire not_1_out;

  assign LDR = WE ? STR : 8'bz;  // Controlled_Buffer controlled_buffer_1
  not not_1 (not_1_out, WE);
  RAM ram_1 (.addr(Address), .data(LDR), .clk(CLK), .ld(not_1_out));  // open: sel, clr

  // Notes on the sheet:
  //   ADD: [000][DR][SR1][00][SR2]
  //   ADD: [001][DR][SR1][imm3]
  //   AND: [010][DR][SR1][00][SR2]
  //   AND: [011][DR][SR1][imm3]
  //   SUB: [100][DR][SR1][00][SR2]
  //   NOT: [101][DR][SR1][000]
  //   LD: [110][DR][Address4]
  //   ST: [111][SR][Address4]
  //   Anding
  //   Subtracting
  //   Accessible address space of 16
  //   Instructions for adding values at\n0e and 0f and storing in 0d
  //   LD R0, #1110      11001110     ce
  //   LD R1, #1111      11011111     df
  //   ADD R0, R0, R1   000001000   08
  //   ST R0, #1101      11101101     ed
  //   LD R0, #1110      11001110     ce
  //   AND R0, R0, #5   01100101     65
  //   ST R0, #1101      11101101     ed
  //   LD R0, #1110      11001110     ce
  //   LD R1, #1111      11011111     df
  //   SUB R0, R1, R0     10001000    81
  //   ST R0, #1101      11101101     ed
  //   Put these instructions in the top\nrow of memory, then put\nnumbers to add (eg 3 and 4)\nin bottom left two addresses
endmodule

module _8_bit_computer (
  input  Reset,
  output [7:0] out_2
);

  wire CLK, decoder_2_out0, DR, finite_state_machine_1_sr2_select, GateALU, GateMARMUX, GateMDR, GatePC,
       LD_IR, LD_MAR, LD_MDR, LD_PC, LD_REG, SR1, SR2, Write_Enable;
  wire [1:0] Gate;
  wire [2:0] finite_state_machine_1_aluk, LD;
  wire [7:0] _0_3_out_2, _0_4_out, add_1_1_add_out, alu_1_output, controlled_buffer_1_out, ir_1_ir_out,
       mar_1_out_4, mdr_1_read_out, mdr_1_write_out, memory_1_ldr, multiplexer_1_out, pc_1_pc_out,
       register_file_1_sr1_out, register_file_1_sr2_out;

  Clock clock_1 (.out(CLK));
  assign controlled_buffer_1_out = GateMDR ? mdr_1_read_out : 8'bz;  // Controlled_Buffer controlled_buffer_1
  MDR mdr_1 (
    .LD_MDR(LD_MDR), .Read_In(memory_1_ldr), .Write_In(controlled_buffer_1_out), .Read_Out(mdr_1_read_out),
    .Write_Out(mdr_1_write_out), .CLK(CLK));
  assign controlled_buffer_1_out = GateMARMUX ? _0_4_out : 8'bz;  // Controlled_Buffer controlled_buffer_2
  Zero_Extend_8____4____8 _0_4 (.In(ir_1_ir_out), .Out(_0_4_out));
  IR ir_1 (.LD_IR(LD_IR), .IR_Out(ir_1_ir_out), .CLK(CLK), .IR_In(controlled_buffer_1_out));
  Cycle_Counter cycle_counter_1 (.CLK(CLK), .Reset(Reset), .out_3(out_2));
  Memory memory_1 (.STR(mdr_1_write_out), .LDR(memory_1_ldr), .Address(mar_1_out_4), .WE(Write_Enable), .CLK(CLK));
  Zero_Extend_8__3__8 _0_3 (.in_1(ir_1_ir_out), .out_2(_0_3_out_2));
  Finite_State_Machine finite_state_machine_1 (
    .Instruction(ir_1_ir_out), .SR2_Select(finite_state_machine_1_sr2_select), .Gate_Code(Gate),
    .LD_Code(LD), .ALUK(finite_state_machine_1_aluk), .CLK(CLK), .DR_SR1_SR2({DR, SR1, SR2}),
    .R_W(Write_Enable));  // open: R, Logic
  MAR mar_1 (.CLK(CLK), .Address(controlled_buffer_1_out), .out_4(mar_1_out_4), .LD_MAR(LD_MAR));
  assign controlled_buffer_1_out = GatePC ? pc_1_pc_out : 8'bz;  // Controlled_Buffer controlled_buffer_3
  PC pc_1 (.LD_PC(LD_PC), .PC_Out(pc_1_pc_out), .CLK(CLK), .PC_In(add_1_1_add_out));  // open: RST
  Add_1 add_1_1 (.Add_in(pc_1_pc_out), .Add_out(add_1_1_add_out));
  Decoder #(.select(2), .enable("false")) decoder_1 (
    .out0(GatePC), .out1(GateMDR), .out2(GateALU), .out3(GateMARMUX), .sel(Gate));
  Register_File register_file_1 (
    .Input(controlled_buffer_1_out), .DR(DR), .CLK(CLK), .LD_REG(LD_REG), .SR2(SR2), .SR1(SR1),
    .SR2_OUT(register_file_1_sr2_out), .SR1_OUT(register_file_1_sr1_out));
  Decoder #(.select(3), .enable("false")) decoder_2 (
    .out0(decoder_2_out0), .out1(LD_MDR), .out2(LD_IR), .out3(LD_REG), .out7(LD_PC), .sel(LD));  // open: out4, out5, out6
  Multiplexer #(.width(8), .disabled(0), .enable("false")) multiplexer_1 (
    .in0(register_file_1_sr2_out), .in1(_0_3_out_2), .out(multiplexer_1_out),
    .sel(finite_state_machine_1_sr2_select));
  ALU alu_1 (
    .ALUK(finite_state_machine_1_aluk), .SR2(multiplexer_1_out), .SR1(register_file_1_sr1_out),
    .Output(alu_1_output));
  assign controlled_buffer_1_out = GateALU ? alu_1_output : 8'bz;  // Controlled_Buffer controlled_buffer_4
  or or_1 (LD_MAR, LD_PC, decoder_2_out0);

  // Notes on the sheet:
  //   2. MDR is loaded with M[MAR]
  //   No MARMUX needed
  //   because LD & ST addr
  //   comes directly from last
  //   four bits
  //   3. Load IR with MDR contents
  //   1. MAR is loaded
  //   No BR or JMP instruction
  //   so no PC MUX needed
  //   1. PC is gated and incremented
  //   4-6: Depends on instruction (see README)
endmodule

module MDR (
  input  [7:0] Write_In,
  input  LD_MDR,
  input  CLK,
  input  [7:0] Read_In,
  output [7:0] Read_Out,
  output [7:0] Write_Out
);

  Register register_1 (.D(Read_In), .en(LD_MDR), .Q(Read_Out), .clk(CLK));  // open: clr
  Register register_2 (.D(Write_In), .Q(Write_Out), .clk(CLK));  // open: en, clr
endmodule

module MAR (
  input  [7:0] Address,
  input  LD_MAR,
  input  CLK,
  output [7:0] out_4
);

  Register register_1 (.D(Address), .en(LD_MAR), .Q(out_4), .clk(CLK));  // open: clr
endmodule

// REG FILE
module Register_File (
  input  [7:0] Input,
  input  DR,
  input  CLK,
  input  LD_REG,
  input  SR2,
  input  SR1,
  output [7:0] SR2_OUT,
  output [7:0] SR1_OUT
);

  wire and_1_out, and_2_out, decoder_1_out0, decoder_1_out1;
  wire [7:0] register_1_q, register_2_q;

  Decoder #(.enable("false")) decoder_1 (.out0(decoder_1_out0), .out1(decoder_1_out1), .sel(DR));
  and and_1 (and_1_out, decoder_1_out0, LD_REG);
  Multiplexer #(.width(8), .disabled(0), .enable("false")) multiplexer_1 (
    .in0(register_1_q), .in1(register_2_q), .out(SR2_OUT), .sel(SR2));
  Register register_1 (.D(Input), .en(and_1_out), .Q(register_1_q), .clk(CLK));  // open: clr
  Register register_2 (.D(Input), .en(and_2_out), .Q(register_2_q), .clk(CLK));  // open: clr
  and and_2 (and_2_out, decoder_1_out1, LD_REG);
  Multiplexer #(.width(8), .disabled(0), .enable("false")) multiplexer_2 (
    .in0(register_1_q), .in1(register_2_q), .out(SR1_OUT), .sel(SR1));
endmodule

module ALU (
  input  [7:0] SR2,
  input  [7:0] SR1,
  input  [2:0] ALUK,
  output [7:0] Output
);

  wire [7:0] AddOut, AND, NOT, not_1_out, SubOut;

  Adder adder_1 (.a(SR1), .b(SR2), .out(AddOut), .cin(1'b0));  // open: cout
  assign not_1_out = ~SR2;  // NOT_Gate not_1, 8 bits wide
  Adder adder_2 (.a(SR1), .b(not_1_out), .out(SubOut), .cin(1'b1));  // open: cout
  assign AND = SR1 & SR2;  // AND_Gate and_1, 8 bits wide
  Multiplexer #(.select(3), .width(8), .disabled(0), .enable("false")) multiplexer_1 (
    .in0(AddOut), .in1(AddOut), .in2(AND), .in3(AND), .in4(SubOut), .in5(NOT), .in6(SR1), .in7(SR1),
    .out(Output), .sel(ALUK));
  assign NOT = ~SR1;  // NOT_Gate not_2, 8 bits wide

  // Other names for the same wires on the sheet: A[7:0] = SR1; B[7:0] = SR2

  // Notes on the sheet:
  //   ADDITION
  //   SUBTRACTION
  //   AND
  //   For Storing R1
  //   NOT
endmodule

module PC (
  input  LD_PC,
  input  CLK,
  input  [7:0] PC_In,
  input  RST,
  output [7:0] PC_Out
);

  Register register_1 (.D(PC_In), .en(LD_PC), .Q(PC_Out), .clk(CLK), .clr(RST));
endmodule

module Add_1 (
  input  [7:0] Add_in,
  output [7:0] Add_out
);

  Adder adder_1 (.a(Add_in), .b({8{1'b0}}), .out(Add_out), .cin(1'b1));  // open: cout
endmodule

// Clock Cycle Counter
module Cycle_Counter (
  input  CLK,
  input  Reset,
  output [7:0] out_3
);

  wire [7:0] add_1_1_add_out;

  Add_1 add_1_1 (.Add_in(out_3), .Add_out(add_1_1_add_out));
  Register register_1 (.D(add_1_1_add_out), .Q(out_3), .clk(CLK), .clr(Reset));  // open: en
endmodule

// Finite \nState \nMachine
module Finite_State_Machine (
  input  [7:0] Instruction,
  input  R,
  input  CLK,
  input  Logic,
  output SR2_Select,
  output [1:0] Gate_Code,
  output [2:0] LD_Code,
  output [2:0] DR_SR1_SR2,
  output [2:0] ALUK,
  output R_W
);

  wire ALU_out, and_4_out, LD_out, LD_ST_out, OFF_out, or_2_out, or_3_out, or_4_out, or_5_out, ST_out;
  wire [7:0] Next_State;
  wire [8:0] Cur_State;

  nor OFF (OFF_out, Cur_State[8], Cur_State[7], Cur_State[6], Cur_State[5], Cur_State[4], Cur_State[3], Cur_State[2], Cur_State[1], Cur_State[0]);
  not ALU (ALU_out, LD_ST_out);
  and LD_ST (LD_ST_out, Instruction[7], Instruction[6]);
  and ST (ST_out, LD_ST_out, Instruction[5]);
  and LD (LD_out, LD_ST_out, ~Instruction[5]);  // AND_Gate
  Register #(.width(9)) register_1 (
    .D({Cur_State[7], Next_State[7], Cur_State[5], Next_State[5:3], Cur_State[1:0], Next_State[0]}),
    .en(1'b1), .Q(Cur_State), .clk(CLK));  // open: clr
  and and_1 (R_W, Instruction[5], Instruction[6], Instruction[7], Cur_State[7]);
  or or_1 (Next_State[0], OFF_out, Cur_State[3], Cur_State[6], Cur_State[8]);
  and ALU_2 (Next_State[3], ALU_out, Cur_State[2]);
  and MEM (Next_State[4], Cur_State[2], LD_ST_out);
  and and_2 (Next_State[5], LD_out, Cur_State[4]);
  and and_3 (Next_State[7], Cur_State[4], ST_out);
  and and_4 (and_4_out, Instruction[5], Instruction[6], Instruction[7]);
  Multiplexer #(.disabled(0), .enable("false")) multiplexer_1 (
    .in0(Instruction[3]), .in1(Instruction[4]), .out(DR_SR1_SR2[1]), .sel(and_4_out));
  or or_2 (or_2_out, Next_State[7], Next_State[3]);
  or or_3 (or_3_out, Cur_State[1], Cur_State[5]);
  or or_4 (or_4_out, Cur_State[0], Next_State[5], Next_State[7]);
  or or_5 (or_5_out, Next_State[3], Cur_State[5]);
  _4_Bit_Encoder u_4_bit_encoder_1 (
    ._0(Next_State[0]), .in_2(or_3_out), .in_3(or_2_out), .in_4(Next_State[4]), .out_5(Gate_Code[0]),
    .out_6(Gate_Code[1]));
  _8_Bit_Encoder u_8_bit_encoder_1 (
    ._0(Next_State[4]), .in_2(or_4_out), .in_3(Cur_State[1]), .in_4(or_5_out), ._0_2(1'b0), .in_6(1'b0),
    .in_7(1'b0), .in_8(Next_State[0]), .out_9(LD_Code[0]), .out_10(LD_Code[1]), .out_11(LD_Code[2]));

  assign ALUK = Instruction[7:5];
  assign {DR_SR1_SR2[2], DR_SR1_SR2[0]} = {Instruction[4], Instruction[0]};
  assign SR2_Select = Instruction[5];

  // Other names for the same wires on the sheet: SR2 = Instruction[0]; DR = Instruction[4];
  //   INSTR[2:0] = Instruction[7:5]; SR1 = Instruction[3];
  //   Next_State (some bits) = {Cur_State[7], Cur_State[5], Cur_State[1:0]}; state9 = Cur_State[7]

  // Notes on the sheet:
  //   ADD: [001][DR][SR1][imm3]
  //   AND: [011][DR][SR1][imm3]
  //   NOT: [101][DR][SR1][000]
  //   ADD: [000][DR][SR1][00][SR2]
  //   AND: [010][DR][SR1][00][SR2]
  //   SUB: [100][DR][SR1][00][SR2]
  //   LD: [110][DR][Address4]
  //   ST: [111][SR][Address4]
  //   Reduced state is a pain to figure out... so this is one-hot
  //   0 for R2, 1 for imm3
  //   00: GatePC
  //   01: GateMDR
  //   10: GateALU
  //   11: GateMARMUX
  //   000: LD MAR
  //   001: LD MDR
  //   010: LD IR
  //   011: LD REG
  //   111: LD MAR & LD PC
  //   0 or 1 for ADD
  //   10 or 11 for AND
  //   100 for SUB
  //   101 for NOT
  //   0 for Read\n1 for Write
  //   4: ALU->DR
  //   States:
  //   1: PC->MAR
  //   2: M[MAR]->MDR
  //   3: MDR->IR
  //   7: MDR->DR
  //   5: imm4 -> MAR
  //   6: M[MAR]->MDR
  //   8: SR->MDR
  //   9: MDR->M[MAR]
endmodule

module IR (
  input  LD_IR,
  input  CLK,
  input  [7:0] IR_In,
  output [7:0] IR_Out
);

  Register register_1 (.D(IR_In), .en(LD_IR), .Q(IR_Out), .clk(CLK));  // open: clr
endmodule

// ZEXT
module Zero_Extend_8__3__8 (
  input  [7:0] in_1,
  output [7:0] out_2
);


  assign out_2 = {{5{1'b0}}, in_1[2:0]};
endmodule

// ZEXT
module Zero_Extend_8____4____8 (
  input  [7:0] In,
  output [7:0] Out
);


  assign Out = {4'b0000, In[3:0]};
endmodule

module _4_Bit_Encoder (
  input  _0,
  input  in_2,
  input  in_3,
  input  in_4,
  output out_5,
  output out_6
);

  or or_1 (out_5, in_2, in_4);
  or or_2 (out_6, in_3, in_4);
endmodule

module _8_Bit_Encoder (
  input  _0,
  input  in_2,
  input  in_3,
  input  in_4,
  input  _0_2,
  input  in_6,
  input  in_7,
  input  in_8,
  output out_9,
  output out_10,
  output out_11
);

  or or_1 (out_10, in_7, in_3, in_4, in_8);
  or or_2 (out_9, in_8, in_2, in_4, in_6);
  or or_3 (out_11, in_8, in_7, in_6, _0_2);
endmodule
